// Logisim project Parking System.circ as structural Verilog: 2 circuits, main circuit main
module main (
);

  wire decoder_1_out0, decoder_1_out1, decoder_1_out2, decoder_1_out3, decoder_1_out4, decoder_1_out5,
       decoder_1_out6, Enter_out, Exit_out, nand_1_out, not_1_out, or_1_out;
  wire [3:0] counter_1_q;

  Button Exit (.out(Exit_out));
  Button Enter (.out(Enter_out));
  or or_1 (or_1_out, Exit_out, Enter_out);
  Counter #(.width(4), .max('h9), .ongoal("stay")) counter_1 (
    .load(Exit_out), .Q(counter_1_q), .clk(or_1_out));  // open: D, count, carry, clr
  Decoder decoder_1 (
    .D(counter_1_q[0]), .C(counter_1_q[1]), .B(counter_1_q[2]), .A(counter_1_q[3]), .OUT0(decoder_1_out0),
    .OUT1(decoder_1_out1), .OUT2(decoder_1_out2), .OUT3(decoder_1_out3), .OUT4(decoder_1_out4),
    .OUT5(decoder_1_out5), .OUT6(decoder_1_out6));
  nand nand_1 (nand_1_out, counter_1_q[0], counter_1_q[3]);
  LED led_1 (.in(nand_1_out));
  LED led_2 (.in(not_1_out));
  not not_1 (not_1_out, nand_1_out);
  _7_Segment_Display u_7_segment_display_1 (
    .g(decoder_1_out6), .f(decoder_1_out5), .a(decoder_1_out0), .b(decoder_1_out1), .e(decoder_1_out4),
    .d(decoder_1_out3), .c(decoder_1_out2));  // open: dp

  // Notes on the sheet:
  //   Available
  //   Full
  //   Done By
  //   Parking Lot Counter System
  //   Muhamed Abdelmaboud ,Mohamed Hassan, Youseif Mansour
  //   we used NAND gate and NOT gate to control the Avaliable and Full lights
  //   this project count the number of cars in the parking and show if its avaliable or full.
  //     we use two input, one for entry and one for exit, there connected to OR gate wich detect any movement.
  //     the counter keep track of how many cars is inside and the number displayed on 7-segment display.
  //    when theres space the green light turn on, and when its completly full the Full light turn on.
endmodule

module Decoder (
  input  D,
  input  C,
  input  B,
  input  A,
  output OUT0,
  output OUT1,
  output OUT2,
  output OUT3,
  output OUT4,
  output OUT5,
  output OUT6
);

  wire and_1_out, and_2_out, and_3_out, and_4_out, and_5_out, and_6_out, and_7_out, and_8_out, and_9_out,
       and_10_out, and_11_out, and_12_out, and_13_out, and_14_out, and_15_out, and_16_out, not_1_out,
       not_2_out, not_3_out, not_4_out, not_5_out, not_6_out, not_7_out, not_8_out, not_9_out, not_10_out,
       not_11_out, not_12_out, not_13_out, not_14_out, not_15_out, not_16_out, not_17_out, not_18_out,
       not_19_out, not_20_out, not_21_out;

  not not_1 (not_1_out, B);
  not not_2 (not_2_out, C);
  not not_3 (not_3_out, D);
  not not_4 (not_4_out, B);
  not not_5 (not_5_out, D);
  not not_6 (not_6_out, B);
  not not_7 (not_7_out, D);
  not not_8 (not_8_out, B);
  not not_9 (not_9_out, D);
  not not_10 (not_10_out, D);
  not not_11 (not_11_out, D);
  not not_12 (not_12_out, C);
  not not_13 (not_13_out, C);
  not not_14 (not_14_out, D);
  not not_15 (not_15_out, B);
  not not_16 (not_16_out, D);
  not not_17 (not_17_out, C);
  not not_18 (not_18_out, D);
  and and_1 (and_1_out, not_2_out, not_3_out);
  and and_2 (and_2_out, C, D);
  and and_3 (and_3_out, not_4_out, not_5_out);
  and and_4 (and_4_out, not_6_out, C);
  and and_5 (and_5_out, C, not_7_out);
  and and_6 (and_6_out, B, not_19_out, D);
  not not_19 (not_19_out, C);
  and and_7 (and_7_out, not_8_out, not_9_out);
  and and_8 (and_8_out, not_10_out, C);
  and and_9 (and_9_out, not_11_out, not_12_out);
  and and_10 (and_10_out, B, not_13_out);
  and and_11 (and_11_out, not_14_out, B);
  and and_12 (and_12_out, not_15_out, C);
  and and_13 (and_13_out, not_16_out, C);
  and and_14 (and_14_out, not_17_out, B);
  and and_15 (and_15_out, not_1_out, not_18_out);
  and and_16 (and_16_out, B, D);
  not not_20 (not_20_out, B);
  not not_21 (not_21_out, C);
  or or_1 (OUT0, and_15_out, C, and_16_out, A);
  or or_2 (OUT1, not_20_out, and_1_out, and_2_out);
  or or_3 (OUT2, not_21_out, D, B);
  or or_4 (OUT4, and_7_out, and_8_out);
  or or_5 (OUT5, and_9_out, and_10_out, and_11_out, A);
  or or_6 (OUT6, and_12_out, and_13_out, and_14_out, A);
  or or_7 (OUT3, and_3_out, and_4_out, and_5_out, and_6_out, A);
endmodule
