// Logisim project parking_counter.circ as structural Verilog: 1 circuit, main circuit main
module main (
);

  wire and_1_out, ENTER__Up_out, EXIT__Down_out, not_1_out, RESET_out;
  wire [0:0] comparator_1_lt;
  wire [3:0] CAR_COUNT_p2;

  Button ENTER__Up (.out(ENTER__Up_out));
  Button EXIT__Down (.out(EXIT__Down_out));
  Button RESET (.out(RESET_out));
  // AND_Gate and_1 has open pins: out=and_1_out
  // NOT_Gate not_1 has open pins: in=open, out=not_1_out
  // Counter #(.width(4), .max(15)) CAR_COUNT: pin names not known; wires that end beside it: and_1_out, CAR_COUNT_p2, EXIT__Down_out, RESET_out
  Comparator #(.width(4), .\unsigned ("true")) comparator_1 (
    .gt(CAR_COUNT_p2[0]), .eq(not_1_out), .lt(comparator_1_lt[0]));  // open: a, b
  // NOT_Gate not_2 has open pins: in=open, out=not_1_out
  Hex_Digit_Display Cars_Inside (.value(CAR_COUNT_p2));  // open: dp
  LED FULL (.in(not_1_out));
  LED Available (.in(not_1_out));
  // Pins of 1 and 4 bits meet at CAR_COUNT_p2
  // Pins of 1 and 4 bits meet at {3'b101, comparator_1_lt[0]}
  // also tied to GND on the sheet: comparator_1_lt[0]
endmodule
